# Fritzing sketch Analog_16_Inputs (saved by Fritzing 0.4.3b)
breadboards: 5

parts:
  Beat707_SV2_Header = female pin header, 4 pins [form="♀ (female)"]
  SV2(Bottom) = female pin header, 4 pins [form="♀ (female)"]  # not connected
  SV3 = female pin header, 4 pins [form="♀ (female)"]  # not connected
  SV3(RIGHT) = female pin header, 4 pins [form="♀ (female)"]
  SV1(Right) = female pin header, 4 pins [form="♀ (female)"]
  SV1 = female pin header, 4 pins [form="♀ (female)"]
  U1 = 74HC595 [package="DIP16 [THT]"]
  R1 = Rotary Potentiometer (Small)
  R2 = Rotary Potentiometer (Small)
  R3 = Rotary Potentiometer (Small)
  R4 = Rotary Potentiometer (Small)
  R5 = Rotary Potentiometer (Small)
  R6 = Rotary Potentiometer (Small)
  R7 = Rotary Potentiometer (Small)
  R8 = Rotary Potentiometer (Small)
  C4067_Multiplexer = IC, DIP package, 24 pins [chip_label="C4067 Multiplexer" spacing=300mil]
  R16 = Rotary Potentiometer (Small)
  R15 = Rotary Potentiometer (Small)
  R14 = Rotary Potentiometer (Small)
  R13 = Rotary Potentiometer (Small)
  R12 = Rotary Potentiometer (Small)
  R11 = Rotary Potentiometer (Small)
  R10 = Rotary Potentiometer (Small)
  R9 = Rotary Potentiometer (Small)
  74HC165N = IC, DIP package, 16 pins [chip_label=74HC165N spacing=300mil]
  R17 = 1k Ω Resistor [package=THT]
  Mixer = Red LED - 5mm
  R17_2 = 1k Ω Resistor [package=THT]
  S1 = Red LED - 5mm
  S2 = Red LED - 5mm
  Octave = Red LED - 5mm
  R17_3 = 1k Ω Resistor [package=THT]
  R17_4 = 1k Ω Resistor [package=THT]
  R17_5 = 10k Ω Resistor [package=THT]
  R17_6 = 10k Ω Resistor [package=THT]
  R17_7 = 10k Ω Resistor [package=THT]
  R17_8 = 10k Ω Resistor [package=THT]
  R17_9 = 10k Ω Resistor [package=THT]
  R17_10 = 10k Ω Resistor [package=THT]
  R17_11 = 10k Ω Resistor [package=THT]
  R17_12 = 10k Ω Resistor [package=THT]
  74HC165N_2 = IC, DIP package, 16 pins [chip_label=74HC165N spacing=300mil]
  R17_13 = 10k Ω Resistor [package=THT]
  R17_14 = 10k Ω Resistor [package=THT]
  R17_15 = 10k Ω Resistor [package=THT]
  R17_16 = 10k Ω Resistor [package=THT]
  R17_17 = 10k Ω Resistor [package=THT]
  R17_18 = 10k Ω Resistor [package=THT]
  R17_19 = 10k Ω Resistor [package=THT]
  R17_20 = 10k Ω Resistor [package=THT]
  R17_21 = 10k Ω Resistor [package=THT]
  Mixer_2 = Pushbutton [package="[THT]"]
  S1_2 = Pushbutton [package="[THT]"]
  S2_2 = Pushbutton [package="[THT]"]
  Octave_2 = Pushbutton [package="[THT]"]
  Encoder_1 = Rotary Potentiometer (Small)
  Encoder_2 = Rotary Potentiometer (Small)
  Encoder_3 = Rotary Potentiometer (Small)
  Encoder_4 = Rotary Potentiometer (Small)
  Encoder_5 = Rotary Potentiometer (Small)
  Encoder_6 = Rotary Potentiometer (Small)

nets:
  N1: Beat707_SV2_Header.pin1, C4067_Multiplexer.pin1
  N2: SV3(RIGHT).pin1, U1.GND, U1.OE, C4067_Multiplexer.pin12, C4067_Multiplexer.pin15, 74HC165N.pin8, 74HC165N.pin10, 74HC165N.pin15, Mixer.cathode, S1.cathode, S2.cathode, Octave.cathode, 74HC165N_2.pin8, 74HC165N_2.pin15, Mixer_2.Pin_3, Mixer_2.Pin_4, S1_2.Pin_3, S1_2.Pin_4, S2_2.Pin_3, S2_2.Pin_4, Octave_2.Pin_3, Octave_2.Pin_4, Encoder_1.wiper, Encoder_2.wiper, Encoder_3.wiper, Encoder_4.wiper, Encoder_5.wiper, Encoder_6.wiper
  N3: SV3(RIGHT).pin4, U1.ST_CP, 74HC165N.pin1, 74HC165N_2.pin1
  N4: SV1(Right).pin1, R17_13.Pin_0
  N5: SV1(Right).pin2, U1.MR
  N6: SV1(Right).pin4, U1.VCC, C4067_Multiplexer.pin24, 74HC165N.pin16, R17_5.Pin_1, R17_6.Pin_1, R17_7.Pin_1, R17_8.Pin_1, R17_9.Pin_0, R17_10.Pin_0, R17_11.Pin_0, R17_12.Pin_0, 74HC165N_2.pin16, R17_14.Pin_1, R17_15.Pin_1, R17_16.Pin_1, R17_17.Pin_1, R17_18.Pin_0, R17_19.Pin_0, R17_20.Pin_0, R17_21.Pin_0
  N7: SV1.pin1, U1.DS
  N8: SV1.pin2, U1.SH_CP, 74HC165N.pin2, 74HC165N_2.pin2
  N9: U1.Q1, R17_2.Pin_0
  N10: U1.Q2, R17_3.Pin_0
  N11: U1.Q3, R17_4.Pin_0
  N12: U1.Q4, C4067_Multiplexer.pin13
  N13: U1.Q5, C4067_Multiplexer.pin14
  N14: U1.Q6, C4067_Multiplexer.pin11
  N15: U1.Q7, C4067_Multiplexer.pin10
  N16: U1.Q0, R17.Pin_0
  N17: R1.wiper, C4067_Multiplexer.pin9
  N18: R2.wiper, C4067_Multiplexer.pin8
  N19: R3.wiper, C4067_Multiplexer.pin7
  N20: R4.wiper, C4067_Multiplexer.pin6
  N21: R5.wiper, C4067_Multiplexer.pin5
  N22: R6.wiper, C4067_Multiplexer.pin4
  N23: R7.wiper, C4067_Multiplexer.pin3
  N24: R8.wiper, C4067_Multiplexer.pin2
  N25: C4067_Multiplexer.pin16, R16.wiper
  N26: C4067_Multiplexer.pin17, R15.wiper
  N27: C4067_Multiplexer.pin18, R14.wiper
  N28: C4067_Multiplexer.pin19, R13.wiper
  N29: C4067_Multiplexer.pin20, R12.wiper
  N30: C4067_Multiplexer.pin21, R11.wiper
  N31: C4067_Multiplexer.pin22, R10.wiper
  N32: C4067_Multiplexer.pin23, R9.wiper
  N33: 74HC165N.pin3, R17_9.Pin_1, Encoder_1.leg2
  N34: 74HC165N.pin4, R17_10.Pin_1, Encoder_1.leg1
  N35: 74HC165N.pin5, R17_11.Pin_1, Encoder_2.leg2
  N36: 74HC165N.pin6, R17_12.Pin_1, Encoder_2.leg1
  N37: 74HC165N.pin9, 74HC165N_2.pin10
  N38: 74HC165N.pin11, R17_8.Pin_0, Octave_2.Pin_1, Octave_2.Pin_2
  N39: 74HC165N.pin12, R17_7.Pin_0, S2_2.Pin_1, S2_2.Pin_2
  N40: 74HC165N.pin13, R17_6.Pin_0, S1_2.Pin_1, S1_2.Pin_2
  N41: 74HC165N.pin14, R17_5.Pin_0, Mixer_2.Pin_1, Mixer_2.Pin_2
  N42: R17.Pin_1, Mixer.anode
  N43: R17_2.Pin_1, S1.anode
  N44: S2.anode, R17_3.Pin_1
  N45: Octave.anode, R17_4.Pin_1
  N46: 74HC165N_2.pin3, R17_18.Pin_1, Encoder_3.leg2
  N47: 74HC165N_2.pin4, R17_19.Pin_1, Encoder_3.leg1
  N48: 74HC165N_2.pin5, R17_20.Pin_1, Encoder_4.leg2
  N49: 74HC165N_2.pin6, R17_21.Pin_1, Encoder_4.leg1
  N50: 74HC165N_2.pin9, R17_13.Pin_1
  N51: 74HC165N_2.pin11, R17_17.Pin_0, Encoder_6.leg2
  N52: 74HC165N_2.pin12, R17_16.Pin_0, Encoder_6.leg1
  N53: 74HC165N_2.pin13, R17_15.Pin_0, Encoder_5.leg2
  N54: 74HC165N_2.pin14, R17_14.Pin_0, Encoder_5.leg1
